# Fritzing sketch dht-lipo-start (saved by Fritzing 0.9.3b)
circuit board: 8.46667cm x 5.64444cm
breadboards: 1

parts:
  DHT1 = DHT22 Humidity and Temperature Sensor
  U1 = LIPO-110mAh [package=lipo-110]
  R1 = Resistor [tolerance=±5% resistance=3.3k package="2010 [SMD]"]
  IC1 = V_REG_LD1117VXX [package=78xxl]
  C1 = Capacitor [part_number=1uF package=cap-pth-small2]
  Espessif_Serial_Wifi_Modul_1 = ESP8266 ESP01 [part_number=ESP8266 package=THT]
  C2 = Capacitor [part_number=1uF package=cap-pth-small2]
  DS1 = DS18B20 1-Wire Temperature Sensor [part_number=DS18B20]
  R2 = Resistor [tolerance=±5% resistance=4.7k package="2512 [SMD]"]

nets:
  VDD: DHT1.VDD, R1.Pin_1, IC1.OUT, C1.1, Espessif_Serial_Wifi_Modul_1.VCC, DS1.VDD, R2.Pin_1
  N1: DHT1.DATA, Espessif_Serial_Wifi_Modul_1.GPIO00
  GND: DHT1.GND, U1.-, IC1.GND, Espessif_Serial_Wifi_Modul_1.GND, C2.1, DS1.GND
  N2: U1.+, IC1.IN, C2.2
  N3: R1.Pin_0, Espessif_Serial_Wifi_Modul_1.CH_PD
  N4: Espessif_Serial_Wifi_Modul_1.GPIO02, DS1.DQ, R2.Pin_0

custom parts:
  ESP8266 ESP01: Generic WiFi Module based on the ESP8266 with onboard PCB antenna and UART communications
